// Logisim project BigASM.circ as structural Verilog
module BOARD_BIG_ASM (
  output out_1
);

  wire button_1_out, CLK, CLR, d_ff_1_q, not_1_out, Write, Write_ASCII;
  wire [6:0] ASCII;
  wire [7:0] counter_1_q;
  wire [23:0] Dir_INPUT, Dir_MEMORY;
  wire [31:0] INPUT, MEMORY_IN, MEMORY_OUT;

  Button button_1 (.out(button_1_out));
  Clock clock_1 (.out(CLK));
  D_Flip_Flop d_ff_1 (.clk(CLK), .D(1'b1), .Q(d_ff_1_q), .reset(button_1_out));  // open: Qn, preset, en
  D_Flip_Flop d_ff_2 (.clk(CLK), .D(d_ff_1_q), .Qn(CLR), .reset(button_1_out));  // open: Q, preset, en
  BIG_ASM big_asm_1 (
    .DATA_INPUT(INPUT), .MEMORY_IN(MEMORY_OUT), .CLK(CLK), .CLR(CLR), .DIR_INPUT(Dir_INPUT),
    .MEMORY_OUT(MEMORY_IN), .DIR_MEMORY(Dir_MEMORY), .Write_OUTPUT(Write), .ASCII(ASCII),
    .Write_ASCII(Write_ASCII), .END(out_1));
  MEMORY memory_1 (.DIR(Dir_MEMORY), .DATA_IN(MEMORY_IN), .WRITE(Write), .CLK(CLK), .CLR(CLR), .DATA_OUT(MEMORY_OUT));
  INPUT input_1 (.DIR(Dir_INPUT), .CLK(CLK), .DATA_OUT(INPUT));
  Counter counter_1 (.load(1'b0), .count(not_1_out), .Q(counter_1_q), .clk(CLK), .clr(CLR));  // open: D, carry
  not not_1 (not_1_out, out_1);
  // Probe on counter_1_q
  TTY #(.rows(32), .cols(60)) tty_1 (.data(ASCII), .clk(CLK), .we(Write_ASCII), .clr(CLR));

  // Other names for the same wires on the sheet: END = out_1

  // Notes on the sheet:
  //   COUNTER
  //   BOARD
endmodule

module INPUT (
  input  [23:0] DIR,
  input  CLK,
  output [31:0] DATA_OUT
);

  RAM #(.addrWidth(24), .dataWidth(32)) ram_1 (.addr(DIR), .data(DATA_OUT), .clk(CLK), .ld(1'b1));  // open: sel, clr
endmodule

module MEMORY (
  input  [23:0] DIR,
  input  [31:0] DATA_IN,
  input  WRITE,
  input  CLK,
  input  CLR,
  output [31:0] DATA_OUT
);

  RAM #(.addrWidth(24), .dataWidth(32), .bus("separate")) ram_1 (
    .addr(DIR), .din(DATA_IN), .data(DATA_OUT), .str(WRITE), .clk(CLK), .clr(CLR));  // open: sel, ld
endmodule

module BIG_ASM (
  input  [31:0] DATA_INPUT,
  input  [31:0] MEMORY_IN,
  input  CLK,
  input  CLR,
  output [23:0] DIR_INPUT,
  output [31:0] MEMORY_OUT,
  output [23:0] DIR_MEMORY,
  output Write_OUTPUT,
  output [6:0] ASCII,
  output Write_ASCII,
  output END
);

  wire END_t, or_1_out, palindrome_1_out_8, palindrome_running, START_PALINDROME;
  wire [23:0] palindrome_1_out_10, var_fin, var_ini;

  PALINDROME palindrome_1 (
    .in_1(var_ini), .in_2(var_fin), .in_3(DATA_INPUT), .in_4(DATA_INPUT), .in_5(CLK),
    .in_6(START_PALINDROME), .in_7(CLR), .out_9(END_t), .out_8(palindrome_1_out_8),
    .out_10(palindrome_1_out_10));
  SUFIX sufix_1 (
    .in_1(DATA_INPUT), .out_6(var_fin), .out_7(var_ini), .in_2(CLK), .in_3(END_t), .in_4(palindrome_1_out_8),
    .in_5(CLR), .out_8(START_PALINDROME), .out_9(END), .out_11(Write_ASCII), .out_10(ASCII));
  or or_1 (or_1_out, END_t, START_PALINDROME);
  D_Flip_Flop d_ff_1 (
    .clk(CLK), .D(palindrome_running), .Qn(palindrome_running), .preset(CLR), .en(or_1_out));  // open: Q, reset
  Multiplexer #(.width(24), .enable("false")) multiplexer_1 (
    .in0(var_ini), .in1(palindrome_1_out_10), .out(DIR_INPUT), .sel(palindrome_running));

  // Other names for the same wires on the sheet: END_SUFIX = END; RESET = CLR
endmodule

module PRINT_UDEC (
  input  [31:0] num,
  input  start,
  input  CLK,
  input  RST,
  output [6:0] ASCII,
  output Write_ASCII,
  output \end 
);

  wire _0_c, _0_n, demultiplexer_1_out0, demultiplexer_2_out0, demultiplexer_2_out1, demultiplexer_3_out0,
       demultiplexer_3_out1, IDLE_2_q, IDLE_3_q, IDLE_4_q, IDLE_q, Lc, Lc_0, Ln, Ln_0, or_1_out;
  wire [23:0] bit_extender_1_out;
  wire [31:0] c, c___1, c___1_t, divider_1_rem, memory_1_data_out, multiplexer_1_out, multiplexer_2_out,
       multiplexer_3_out, n, n___10, n___10___48;

  Multiplexer #(.width(32), .enable("false")) multiplexer_1 (
    .in0(num), .in1(n___10), .out(multiplexer_1_out), .sel(Lc_0));
  Divider #(.width(32)) divider_1 (.a(n), .b(32'ha), .out(n___10), .rem(divider_1_rem));  // open: upper
  Adder #(.width(32)) adder_1 (.a(divider_1_rem), .b(32'h30), .out(n___10___48));  // open: cin, cout
  or or_1 (or_1_out, demultiplexer_1_out0, \end );
  Register #(.width(32)) u_n (.D(multiplexer_1_out), .en(Ln), .Q(n), .clk(CLK), .clr(RST));
  D_Flip_Flop IDLE (.clk(CLK), .D(or_1_out), .Q(IDLE_q), .preset(RST));  // open: Qn, en, reset
  Demultiplexer #(.enable("false")) demultiplexer_1 (
    .out0(demultiplexer_1_out0), .out1(Ln_0), .in(IDLE_q), .sel(start));
  or or_2 (Write_ASCII, demultiplexer_3_out0, demultiplexer_2_out1);
  Multiplexer #(.width(32), .enable("false")) multiplexer_2 (
    .in0(c___1), .in1(c___1_t), .out(multiplexer_2_out), .sel(Write_ASCII));
  Adder #(.width(32)) adder_2 (.a(c), .b(32'h1), .out(c___1));  // open: cin, cout
  Subtractor #(.width(32)) subtractor_1 (.a(c), .b(32'h1), .out(c___1_t));  // open: bin, bout
  D_Flip_Flop IDLE_2 (.clk(CLK), .D(Ln_0), .Q(IDLE_2_q), .reset(RST));  // open: Qn, preset, en
  Register #(.width(32)) u_c (.D(multiplexer_2_out), .en(Lc), .Q(c), .clk(CLK), .clr(RST));
  or or_3 (Lc_0, IDLE_2_q, demultiplexer_3_out1);
  Multiplexer #(.width(32), .enable("false")) multiplexer_3 (
    .in0(c), .in1(c___1_t), .out(multiplexer_3_out), .sel(Write_ASCII));
  Comparator #(.width(32), .mode("unsigned")) comparator_1 (.a({32{1'b0}}), .b(n), .lt(_0_n));  // open: gt, eq
  Comparator #(.width(32), .mode("unsigned")) comparator_2 (.a({32{1'b0}}), .b(c), .lt(_0_c));  // open: gt, eq
  D_Flip_Flop IDLE_3 (.clk(CLK), .D(Write_ASCII), .Q(IDLE_3_q), .reset(RST));  // open: Qn, preset, en
  Demultiplexer #(.enable("false")) demultiplexer_2 (
    .out0(demultiplexer_2_out0), .out1(demultiplexer_2_out1), .in(IDLE_3_q), .sel(_0_c));
  Bit_Extender #(.in_width(32), .out_width(24)) bit_extender_1 (.in(multiplexer_3_out), .out(bit_extender_1_out));
  D_Flip_Flop IDLE_4 (.clk(CLK), .D(Lc_0), .Q(IDLE_4_q), .reset(RST));  // open: Qn, preset, en
  or or_4 (Lc, Lc_0, Write_ASCII);
  or or_5 (Ln, Ln_0, Lc_0);
  Demultiplexer #(.enable("false")) demultiplexer_3 (
    .out0(demultiplexer_3_out0), .out1(demultiplexer_3_out1), .in(IDLE_4_q), .sel(_0_n));
  D_Flip_Flop IDLE_5 (.clk(CLK), .D(demultiplexer_2_out0), .Q(\end ), .reset(RST));  // open: Qn, preset, en
  MEMORY memory_1 (
    .DIR(bit_extender_1_out), .DATA_IN(n___10___48), .WRITE(Lc_0), .CLK(CLK), .CLR(RST),
    .DATA_OUT(memory_1_data_out));
  Bit_Extender #(.in_width(32), .out_width(7)) bit_extender_2 (.in(memory_1_data_out), .out(ASCII));

  // Other names for the same wires on the sheet: Lc_1 = Write_ASCII; Sc = Write_ASCII; Ln_1 = Lc_0; Sn = Lc_0;
  //   Write = Lc_0
endmodule

module PRINT_DEC (
  input  [31:0] num,
  input  start,
  input  CLK,
  input  RST,
  output [6:0] ASCII,
  output Write_ASCII,
  output END
);

  wire demultiplexer_1_out0, demultiplexer_1_out1, demultiplexer_2_out0, demultiplexer_3_out0, end_t,
       IDLE_3_q, IDLE_q, or_1_out, or_2_out, or_3_out, S_ASCII, startUDEC, Write_ASCII_1;
  wire [6:0] ASCII_t;
  wire [31:0] multiplexer_1_out, negator_1_out;

  or or_1 (or_1_out, demultiplexer_1_out0, END);
  Negator #(.width(32)) negator_1 (.in(num), .out(negator_1_out));
  D_Flip_Flop IDLE (.clk(CLK), .D(or_1_out), .Q(IDLE_q), .preset(RST));  // open: Qn, en, reset
  Demultiplexer #(.enable("false")) demultiplexer_1 (
    .out0(demultiplexer_1_out0), .out1(demultiplexer_1_out1), .in(IDLE_q), .sel(start));
  Multiplexer #(.width(32), .enable("false")) multiplexer_1 (
    .in0(num), .in1(negator_1_out), .out(multiplexer_1_out), .sel(num[31]));
  Demultiplexer #(.enable("false")) demultiplexer_2 (
    .out0(demultiplexer_2_out0), .out1(S_ASCII), .in(demultiplexer_1_out1), .sel(num[31]));
  or or_2 (or_2_out, demultiplexer_2_out0, S_ASCII);
  D_Flip_Flop IDLE_2 (.clk(CLK), .D(or_2_out), .Q(startUDEC), .reset(RST));  // open: Qn, preset, en
  PRINT_UDEC print_udec_1 (
    .num(multiplexer_1_out), .start(startUDEC), .CLK(CLK), .RST(RST), .ASCII(ASCII_t),
    .Write_ASCII(Write_ASCII_1), .\end (end_t));
  D_Flip_Flop IDLE_3 (.clk(CLK), .D(or_3_out), .Q(IDLE_3_q), .reset(RST));  // open: Qn, preset, en
  or or_3 (or_3_out, startUDEC, demultiplexer_3_out0);
  Demultiplexer #(.enable("false")) demultiplexer_3 (
    .out0(demultiplexer_3_out0), .out1(END), .in(IDLE_3_q), .sel(end_t));
  Multiplexer #(.width(7), .enable("false")) multiplexer_2 (
    .in0(ASCII_t), .in1(7'b0101101), .out(ASCII), .sel(S_ASCII));
  or or_4 (Write_ASCII, S_ASCII, Write_ASCII_1);

  // Other names for the same wires on the sheet: sign = num[31]; Write_ASCII_0 = S_ASCII
endmodule

module TEST_PRINT (
  input  [31:0] in_1,
  output out_2
);

  wire button_1_out, button_2_out, CLK, CLR, d_ff_1_q, Write_ASCII;
  wire [6:0] ASCII;

  Button button_1 (.out(button_1_out));
  Clock clock_1 (.out(CLK));
  D_Flip_Flop d_ff_1 (.clk(CLK), .D(1'b1), .Q(d_ff_1_q), .reset(button_1_out));  // open: Qn, preset, en
  D_Flip_Flop d_ff_2 (.clk(CLK), .D(d_ff_1_q), .Qn(CLR), .reset(button_1_out));  // open: Q, preset, en
  Button button_2 (.out(button_2_out));
  PRINT_UDEC print_udec_1 ();  // open: num, start, CLK, RST, ASCII, Write_ASCII, end
  PRINT_DEC print_dec_1 (
    .num(in_1), .start(button_2_out), .CLK(CLK), .RST(CLR), .ASCII(ASCII), .Write_ASCII(Write_ASCII),
    .END(out_2));
  TTY #(.rows(32), .cols(60)) tty_1 (.data(ASCII), .clk(CLK), .we(Write_ASCII), .clr(CLR));
endmodule

module DATA_PATH_ES_PAL (
  input  in_1,
  input  [23:0] in_2,
  input  in_3,
  input  in_4,
  input  [23:0] in_5,
  input  in_6,
  input  [31:0] in_7,
  input  in_8,
  input  [31:0] in_9,
  input  in_10,
  input  in_11,
  input  in_12,
  input  in_13,
  output out_14,
  output out_15,
  output out_16,
  output [23:0] out_17,
  output [23:0] out_18
);

  wire comparator_2_eq;
  wire [23:0] fin_1, ini_1, multiplexer_1_out, multiplexer_2_out;
  wire [31:0] arr_fin, arr_ini;

  Multiplexer #(.width(24), .enable("false")) multiplexer_1 (
    .in0(in_2), .in1(ini_1), .out(multiplexer_1_out), .sel(in_1));
  Multiplexer #(.width(24), .enable("false")) multiplexer_2 (
    .in0(in_5), .in1(fin_1), .out(multiplexer_2_out), .sel(in_4));
  Register #(.width(24)) INI (.D(multiplexer_1_out), .en(in_3), .Q(out_17), .clk(in_13));  // open: clr
  Register #(.width(24)) FIN (.D(multiplexer_2_out), .en(in_6), .Q(out_18), .clk(in_13));  // open: clr
  Register #(.width(32)) u_ARR_INI (.D(in_7), .en(in_8), .Q(arr_ini), .clk(in_13));  // open: clr
  Register #(.width(32)) u_ARR_FIN (.D(in_9), .en(in_10), .Q(arr_fin), .clk(in_13));  // open: clr
  D_Flip_Flop d_ff_1 (.clk(in_13), .D(in_11), .Q(out_16), .en(in_12));  // open: Qn, preset, reset
  Adder #(.width(24)) adder_1 (.a(out_17), .b(24'h1), .out(ini_1));  // open: cin, cout
  Subtractor #(.width(24)) subtractor_1 (.a(out_18), .b(24'h1), .out(fin_1));  // open: bin, bout
  Comparator #(.width(24), .mode("unsigned")) comparator_1 (.a(out_17), .b(out_18), .lt(out_14));  // open: gt, eq
  Comparator #(.width(32), .mode("unsigned")) comparator_2 (
    .a(arr_ini), .b(arr_fin), .eq(comparator_2_eq));  // open: gt, lt
  not not_1 (out_15, comparator_2_eq);

  // Other names for the same wires on the sheet: ANSWER = out_16; arr_ini_____arr_fin = out_15; CLK = in_13;
  //   fin[23:0] = out_18; ini[23:0] = out_17; ini_fin = out_14; L_ANSWER = in_12; L_arr_fin = in_10; L_arr_ini = in_8;
  //   L_fin = in_6; L_ini = in_3; S_fin = in_4; S_ini = in_1; SET_ANSWER = in_11; var_arr_fin[31:0] = in_9;
  //   var_arr_ini[31:0] = in_7; var_fin[23:0] = in_5; var_ini[23:0] = in_2

  // Notes on the sheet:
  //   INPUT
  //   OUTPUT
endmodule

module CONTROL_UNIT_ES_PAL (
  input  in_1,
  input  in_2,
  input  in_3,
  input  in_4,
  input  in_5,
  output out_6,
  output out_7,
  output out_8,
  output out_9,
  output out_10,
  output out_11,
  output out_12,
  output out_13,
  output out_14,
  output out_15,
  output out_16
);

  wire d_ff_1_q, demultiplexer_1_out0, demultiplexer_2_out1, demultiplexer_3_out1, L_ANSWER0, L_arr_fin_0,
       L_arr_fin_1, L_arr_ini_0, L_arr_ini_1, or_1_out, or_7_out, or_9_out, WHILE_q;

  or or_1 (or_1_out, demultiplexer_1_out0, out_14);
  D_Flip_Flop d_ff_1 (.clk(in_3), .D(or_1_out), .Q(d_ff_1_q), .preset(in_5));  // open: Qn, en, reset
  or or_2 (out_9, L_ANSWER0, out_8);
  or or_3 (out_11, L_ANSWER0, out_8);
  or or_4 (out_7, L_ANSWER0, out_6);
  or or_5 (out_12, L_arr_ini_0, L_arr_ini_1);
  Demultiplexer #(.enable("false")) demultiplexer_1 (
    .out0(demultiplexer_1_out0), .out1(L_ANSWER0), .in(d_ff_1_q), .sel(in_4));
  D_Flip_Flop LOAD_INI (.clk(in_3), .D(L_ANSWER0), .Q(L_arr_ini_0), .reset(in_5));  // open: Qn, preset, en
  or or_6 (out_13, L_arr_fin_0, L_arr_fin_1);
  D_Flip_Flop LOAD_FIN (.clk(in_3), .D(L_arr_ini_0), .Q(L_arr_fin_0), .reset(in_5));  // open: Qn, preset, en
  or or_7 (or_7_out, L_arr_fin_0, L_arr_fin_1);
  D_Flip_Flop WHILE (.clk(in_3), .D(or_7_out), .Q(WHILE_q), .reset(in_5));  // open: Qn, preset, en
  or or_8 (out_15, L_arr_fin_0, L_arr_fin_1);
  Demultiplexer #(.enable("false")) demultiplexer_2 (
    .out0(out_6), .out1(demultiplexer_2_out1), .in(WHILE_q), .sel(in_1));
  D_Flip_Flop LOAD_INI_2 (.clk(in_3), .D(out_8), .Q(L_arr_ini_1), .reset(in_5));  // open: Qn, preset, en
  or or_9 (or_9_out, out_6, demultiplexer_3_out1);
  D_Flip_Flop END (.clk(in_3), .D(or_9_out), .Q(out_14), .reset(in_5));  // open: Qn, preset, en
  D_Flip_Flop LOAD_FIN_2 (.clk(in_3), .D(L_arr_ini_1), .Q(L_arr_fin_1), .reset(in_5));  // open: Qn, preset, en
  Demultiplexer #(.enable("false")) demultiplexer_3 (
    .out0(out_8), .out1(demultiplexer_3_out1), .in(demultiplexer_2_out1), .sel(in_2));

  assign out_10 = out_8;

  // Other names for the same wires on the sheet: arr_ini_____arr_fin = in_2; CLK = in_3; END = out_14; ini_fin = in_1;
  //   L_address = out_16; L_ANSWER = out_7; ANSWER = out_6; L_ANSWER1 = out_6; L_arr_fin = out_13; L_arr_ini = out_12;
  //   L_fin = out_11; L_ini = out_9; L_fin1 = L_ANSWER0; L_ini1 = L_ANSWER0; RESET = in_5; S_address = out_15;
  //   S_address0 = L_arr_fin_0; S_address1 = L_arr_fin_1; L_fin2 = out_8; L_ini2 = out_8; S_fin = out_8;
  //   S_ini = out_8; START = in_4
endmodule

module PALINDROME (
  input  [23:0] in_1,
  input  [23:0] in_2,
  input  [31:0] in_3,
  input  [31:0] in_4,
  input  in_5,
  input  in_6,
  input  in_7,
  output out_8,
  output out_9,
  output [23:0] out_10
);

  wire arr_ini___arr_fin, control_unit_es_pal_1_out_6, control_unit_es_pal_1_out_7,
       control_unit_es_pal_1_out_8, control_unit_es_pal_1_out_9, control_unit_es_pal_1_out_10,
       control_unit_es_pal_1_out_11, control_unit_es_pal_1_out_12, control_unit_es_pal_1_out_13, ini_fin,
       LOAD_ADDRESS, SELECT_ADDRESS;
  wire [23:0] fin, ini;

  CONTROL_UNIT_ES_PAL control_unit_es_pal_1 (
    .in_1(ini_fin), .in_2(arr_ini___arr_fin), .in_3(in_5), .in_4(in_6), .in_5(in_7),
    .out_6(control_unit_es_pal_1_out_6), .out_7(control_unit_es_pal_1_out_7),
    .out_8(control_unit_es_pal_1_out_8), .out_9(control_unit_es_pal_1_out_9),
    .out_10(control_unit_es_pal_1_out_10), .out_11(control_unit_es_pal_1_out_11),
    .out_12(control_unit_es_pal_1_out_12), .out_13(control_unit_es_pal_1_out_13), .out_14(out_9),
    .out_15(SELECT_ADDRESS), .out_16(LOAD_ADDRESS));
  Multiplexer #(.width(24), .enable("false")) multiplexer_1 (.in0(ini), .in1(fin), .out(out_10), .sel(SELECT_ADDRESS));
  DATA_PATH_ES_PAL data_path_es_pal_1 (
    .in_1(control_unit_es_pal_1_out_8), .in_2(in_1), .in_3(control_unit_es_pal_1_out_11),
    .in_4(control_unit_es_pal_1_out_10), .in_5(in_2), .in_6(control_unit_es_pal_1_out_9), .in_7(in_3),
    .in_8(control_unit_es_pal_1_out_12), .in_9(in_4), .in_10(control_unit_es_pal_1_out_13),
    .in_11(control_unit_es_pal_1_out_6), .in_12(control_unit_es_pal_1_out_7), .in_13(in_5), .out_14(ini_fin),
    .out_15(arr_ini___arr_fin), .out_16(out_8), .out_17(ini), .out_18(fin));

  // Other names for the same wires on the sheet: ANSWER = out_8; CLK = in_5; END = out_9; RESET = in_7; START = in_6;
  //   var_arr_fin[31:0] = in_4; var_arr_ini[31:0] = in_3; var_fin[23:0] = in_2; var_ini[23:0] = in_1

  // Notes on the sheet:
  //   CONECTION  PALINDROME
endmodule

module DATA_PATH (
  input  [23:0] in_1,
  input  [31:0] in_2,
  input  in_3,
  input  in_4,
  input  in_5,
  input  in_6,
  input  in_7,
  input  in_8,
  input  in_9,
  output [23:0] out_10,
  output [23:0] out_11,
  output out_12,
  output out_13,
  output [31:0] out_14
);

  wire [23:0] i_1, i_1_t, multiplexer_1_out;

  Multiplexer #(.select(2), .width(24), .enable("false")) multiplexer_1 (
    .in0(24'h1), .in1(i_1), .in2(i_1_t), .out(multiplexer_1_out), .sel({in_6, in_5}));  // open: in3
  Register #(.width(24)) N (.D(in_1), .en(in_7), .Q(out_10), .clk(in_3), .clr(in_4));
  Register #(.width(24)) i (.D(multiplexer_1_out), .en(in_8), .Q(out_11), .clk(in_3), .clr(in_4));
  Register #(.width(32)) N_2 (.D(in_2), .en(in_9), .Q(out_14), .clk(in_3), .clr(in_4));
  Adder #(.width(24)) adder_1 (.a(out_11), .b(24'h1), .out(i_1));  // open: cin, cout
  Subtractor #(.width(24)) subtractor_1 (.a(out_11), .b(24'h1), .out(i_1_t));  // open: bin, bout
  Comparator #(.width(24), .mode("unsigned")) comparator_1 (.a(out_11), .b(out_10), .lt(out_12));  // open: gt, eq
  Comparator #(.width(24), .mode("unsigned")) comparator_2 (.a(out_11), .b({24{1'b0}}), .gt(out_13));  // open: eq, lt

  // Other names for the same wires on the sheet: Si = in_5; Si_minus_minus = in_6; arr_i[31:0] = in_2; CLK = in_3;
  //   i[23:0] = out_11; i_0 = out_13; i_N = out_12; L_i = in_8; L_N = in_7; L_num = in_9; N[23:0] = out_10;
  //   num[31:0] = out_14; RESET = in_4; var_n[23:0] = in_1
endmodule

module CONTROL_UNIT (
  input  in_1,
  input  in_2,
  input  in_3,
  input  in_4,
  input  in_5,
  input  in_6,
  input  [31:0] in_7,
  output out_8,
  output out_9,
  output out_10,
  output out_11,
  output out_12,
  output out_13,
  output out_14,
  output [6:0] out_15,
  output out_16
);

  wire d_ff_2_q, d_ff_3_q, demultiplexer_1_out0, demultiplexer_2_out0, demultiplexer_2_out1,
       demultiplexer_3_out0, demultiplexer_4_out0, demultiplexer_4_out1, demultiplexer_5_out0,
       demultiplexer_6_out1, demultiplexer_7_out0, demultiplexer_7_out1, demultiplexer_8_out0,
       demultiplexer_8_out1, END_PRINT, or_2_out, or_3_out, or_4_out, or_7_out, or_8_out, or_9_out, PRINT,
       START, START_PRINT, WHILE_2_q, WHILE_3_q, WHILE_5_q, WHILE_q;

  or or_1 (out_12, out_11, out_10, out_9);
  D_Flip_Flop d_ff_1 (.clk(in_1), .D(in_4), .Q(START));  // open: Qn, preset, en, reset
  or or_2 (or_2_out, demultiplexer_1_out0, PRINT);
  or or_3 (or_3_out, demultiplexer_2_out0, demultiplexer_8_out1);
  D_Flip_Flop d_ff_2 (.clk(in_1), .D(or_2_out), .Q(d_ff_2_q), .preset(in_4));  // open: Qn, en, reset
  D_Flip_Flop d_ff_3 (.clk(in_1), .D(or_3_out), .Q(d_ff_3_q), .preset(in_4));  // open: Qn, en, reset
  Demultiplexer #(.enable("false")) demultiplexer_1 (
    .out0(demultiplexer_1_out0), .out1(out_11), .in(d_ff_2_q), .sel(START));
  Demultiplexer #(.enable("false")) demultiplexer_2 (
    .out0(demultiplexer_2_out0), .out1(demultiplexer_2_out1), .in(d_ff_3_q), .sel(PRINT));
  or or_4 (or_4_out, out_10, out_11);
  or or_5 (out_9, demultiplexer_7_out1, demultiplexer_2_out1);
  Demultiplexer #(.enable("false")) demultiplexer_3 (
    .out0(demultiplexer_3_out0), .out1(out_13), .in(WHILE_q), .sel(in_2));
  D_Flip_Flop WHILE (.clk(in_1), .D(or_4_out), .Q(WHILE_q), .reset(in_4));  // open: Qn, preset, en
  D_Flip_Flop dec_i (.clk(in_1), .D(out_9), .Q(out_8), .reset(in_4));  // open: Qn, preset, en
  or or_6 (PRINT, demultiplexer_3_out0, demultiplexer_6_out1);
  or or_7 (or_7_out, demultiplexer_4_out0, out_13);
  PRINT_DEC print_dec_1 (
    .num(in_7), .start(START_PRINT), .CLK(in_1), .RST(in_4), .ASCII(out_15), .Write_ASCII(out_16),
    .END(END_PRINT));
  D_Flip_Flop WHILE_2 (.clk(in_1), .D(out_8), .Q(WHILE_2_q), .reset(in_4));  // open: Qn, preset, en
  Demultiplexer #(.enable("false")) demultiplexer_4 (
    .out0(demultiplexer_4_out0), .out1(demultiplexer_4_out1), .in(WHILE_3_q), .sel(in_5));
  D_Flip_Flop WHILE_3 (.clk(in_1), .D(or_7_out), .Q(WHILE_3_q), .reset(in_4));  // open: Qn, preset, en
  Demultiplexer #(.enable("false")) demultiplexer_5 (
    .out0(demultiplexer_5_out0), .out1(START_PRINT), .in(WHILE_2_q), .sel(in_3));
  or or_8 (or_8_out, demultiplexer_8_out0, demultiplexer_5_out0);
  or or_9 (or_9_out, demultiplexer_7_out0, START_PRINT);
  Demultiplexer #(.enable("false")) demultiplexer_6 (
    .out0(out_10), .out1(demultiplexer_6_out1), .in(demultiplexer_4_out1), .sel(in_6));
  D_Flip_Flop WHILE_4 (.clk(in_1), .D(or_8_out), .Q(out_14), .reset(in_4));  // open: Qn, preset, en
  D_Flip_Flop WHILE_5 (.clk(in_1), .D(or_9_out), .Q(WHILE_5_q), .reset(in_4));  // open: Qn, preset, en
  Demultiplexer #(.enable("false")) demultiplexer_7 (
    .out0(demultiplexer_7_out0), .out1(demultiplexer_7_out1), .in(WHILE_5_q), .sel(END_PRINT));
  Demultiplexer #(.enable("false")) demultiplexer_8 (
    .out0(demultiplexer_8_out0), .out1(demultiplexer_8_out1), .in(out_14), .sel(START));

  // Other names for the same wires on the sheet: ANSWER = in_6; ASCII[6:0] = out_15; CLK = in_1; END = in_5;
  //   END_SUFIX = out_14; i_0 = in_3; i_N = in_2; L_i0 = out_11; L_N = out_11; L_num = out_8; num[31:0] = in_7;
  //   RESET = in_4; L_i1 = out_10; Si = out_10; L_i2 = out_9; Si_minus_minus = out_9; START_PALINDROME = out_13;
  //   Write_ASCII = out_16
endmodule

module SUFIX (
  input  [31:0] in_1,
  input  in_2,
  input  in_3,
  input  in_4,
  input  in_5,
  output [23:0] out_6,
  output [23:0] out_7,
  output out_8,
  output out_9,
  output [6:0] out_10,
  output out_11
);

  wire control_unit_1_out_9, control_unit_1_out_10, control_unit_1_out_11, control_unit_1_out_12,
       data_path_1_out_12, data_path_1_out_13, L_num;
  wire [31:0] num;

  DATA_PATH data_path_1 (
    .in_1(in_1[23:0]), .out_10(out_6), .out_11(out_7), .in_3(in_2), .in_6(control_unit_1_out_9),
    .in_7(control_unit_1_out_11), .in_8(control_unit_1_out_12), .out_12(data_path_1_out_12),
    .in_5(control_unit_1_out_10), .out_13(data_path_1_out_13), .in_2(in_1), .out_14(num), .in_9(L_num),
    .in_4(in_5));
  CONTROL_UNIT control_unit_1 (
    .out_10(control_unit_1_out_10), .out_11(control_unit_1_out_11), .out_12(control_unit_1_out_12),
    .in_1(in_2), .in_2(data_path_1_out_12), .in_4(in_5), .out_14(out_9), .out_13(out_8), .in_5(in_3),
    .in_6(in_4), .out_15(out_10), .out_16(out_11), .out_9(control_unit_1_out_9), .in_3(data_path_1_out_13),
    .in_7(num), .out_8(L_num));

  // Other names for the same wires on the sheet: ANSWER = in_4; arr_i[31:0] = in_1; var_n[23:0] = in_1[23:0];
  //   ASCII[6:0] = out_10; CLK = in_2; END = in_3; END_SUFIX = out_9; i[23:0] = out_7; n[23:0] = out_6; RESET = in_5;
  //   START_PALINDROME = out_8; Write_ASCII = out_11
endmodule
