// Logisim project problem75.circ as structural Verilog
module BOARD_BIG_ASM (
  output out_1
);

  wire button_1_out, CLK, CLR, d_ff_1_q, not_1_out, Write, Write_ASCII;
  wire [6:0] ASCII;
  wire [7:0] counter_1_q;
  wire [23:0] Dir_INPUT, Dir_MEMORY;
  wire [31:0] INPUT, MEMORY_IN, MEMORY_OUT;

  Button button_1 (.out(button_1_out));
  Clock clock_1 (.out(CLK));
  D_Flip_Flop d_ff_1 (.clk(CLK), .D(1'b1), .Q(d_ff_1_q), .reset(button_1_out));  // open: Qn, preset, en
  D_Flip_Flop d_ff_2 (.clk(CLK), .D(d_ff_1_q), .Qn(CLR), .reset(button_1_out));  // open: Q, preset, en
  BIG_ASM big_asm_1 (
    .DATA_INPUT(INPUT), .MEMORY_IN(MEMORY_OUT), .CLK(CLK), .CLR(CLR), .DIR_INPUT(Dir_INPUT),
    .MEMORY_OUT(MEMORY_IN), .DIR_MEMORY(Dir_MEMORY), .Write_OUTPUT(Write), .ASCII(ASCII),
    .Write_ASCII(Write_ASCII), .END(out_1));
  MEMORY memory_1 (.DIR(Dir_MEMORY), .DATA_IN(MEMORY_IN), .WRITE(Write), .CLK(CLK), .CLR(CLR), .DATA_OUT(MEMORY_OUT));
  INPUT input_1 (.DIR(Dir_INPUT), .CLK(CLK), .DATA_OUT(INPUT));
  Counter counter_1 (.load(1'b0), .count(not_1_out), .Q(counter_1_q), .clk(CLK), .clr(CLR));  // open: D, carry
  not not_1 (not_1_out, out_1);
  // Probe on counter_1_q
  TTY #(.rows(32), .cols(60)) tty_1 (.data(ASCII), .clk(CLK), .we(Write_ASCII), .clr(CLR));

  // Other names for the same wires on the sheet: END = out_1

  // Notes on the sheet:
  //   COUNTER
  //   BOARD
endmodule

module INPUT (
  input  [23:0] DIR,
  input  CLK,
  output [31:0] DATA_OUT
);

  RAM #(.addrWidth(24), .dataWidth(32)) ram_1 (.addr(DIR), .data(DATA_OUT), .clk(CLK), .ld(1'b1));  // open: sel, clr
endmodule

module MEMORY (
  input  [23:0] DIR,
  input  [31:0] DATA_IN,
  input  WRITE,
  input  CLK,
  input  CLR,
  output [31:0] DATA_OUT
);

  RAM #(.addrWidth(24), .dataWidth(32), .bus("separate")) ram_1 (
    .addr(DIR), .din(DATA_IN), .data(DATA_OUT), .str(WRITE), .clk(CLK), .clr(CLR));  // open: sel, ld
endmodule

module BIG_ASM (
  input  [31:0] DATA_INPUT,
  input  [31:0] MEMORY_IN,
  input  CLK,
  input  CLR,
  output [23:0] DIR_INPUT,
  output [31:0] MEMORY_OUT,
  output [23:0] DIR_MEMORY,
  output Write_OUTPUT,
  output [6:0] ASCII,
  output Write_ASCII,
  output END
);

  wire _0, _1, _2, and_1_out, Condition, control_unit_1_calculate, not_1_out, Valid;
  wire [1:0] _00;
  wire [31:0] day, day_input, month, month_input, year, year_input;

  Demultiplexer #(.select(2), .width(32), .enable("false")) demultiplexer_1 (
    .out0(day_input), .out1(month_input), .out2(year_input), .in(DATA_INPUT), .sel(_00));  // open: out3
  Data_Path data_path_1 (
    .day(day), .month(month), .year(year), .final_final_true_output(Valid), .Start(control_unit_1_calculate));
  Counter #(.width(2), .max('h3)) counter_1 (.Q(_00), .clk(and_1_out));  // open: load, D, count, carry, clr
  and and_1 (and_1_out, CLK, Condition);
  Multiplexer #(.width(7)) multiplexer_1 (.in0(7'b1000110), .in1(7'b1010100), .out(ASCII), .sel(Valid), .en(END));
  assign DIR_INPUT = {{22{1'b0}}, _00};  // Bit_Extender bit_extender_1
  not not_1 (not_1_out, Condition);
  Comparator #(.width(2), .mode("unsigned")) comparator_1 (.a(_00), .b(2'b11), .lt(Condition));  // open: gt, eq
  Control_Unit control_unit_1 (
    .Start(not_1_out), .rst(CLR), .Calculate(control_unit_1_calculate), .clk(CLK), .End(END));
  Comparator #(.width(2), .mode("unsigned")) comparator_2 (.a(_00), .b(2'b00), .eq(_0));  // open: gt, lt
  Comparator #(.width(2), .mode("unsigned")) comparator_3 (.a(_00), .b(2'b01), .eq(_1));  // open: gt, lt
  Comparator #(.width(2), .mode("unsigned")) comparator_4 (.a(_00), .b(2'b10), .eq(_2));  // open: gt, lt
  Register #(.width(32)) u_day (.D(day_input), .en(_0), .Q(day), .clk(CLK));  // open: clr
  Register #(.width(32)) u_year (.D(month_input), .en(_1), .Q(month), .clk(CLK));  // open: clr
  Register #(.width(32)) u_month (.D(year_input), .en(_2), .Q(year), .clk(CLK));  // open: clr

  assign DIR_MEMORY = {24{1'b0}};
  assign MEMORY_OUT = {32{1'b0}};
  assign Write_ASCII = END;
  assign Write_OUTPUT = 1'b0;

  // Other names for the same wires on the sheet: clock_prime = CLK; Letter[6:0] = ASCII; _11[1:0] = _00;
  //   _22[1:0] = _00; Max[1:0] = _00; Reset = CLR
endmodule

module PRINT_UDEC (
  input  [31:0] num,
  input  start,
  input  CLK,
  input  RST,
  output [6:0] ASCII,
  output Write_ASCII,
  output \end 
);

  wire _0_c, _0_n, demultiplexer_1_out0, demultiplexer_2_out0, demultiplexer_2_out1, demultiplexer_3_out0,
       demultiplexer_3_out1, IDLE_2_q, IDLE_3_q, IDLE_4_q, IDLE_q, Lc, Lc_0, Ln, Ln_0, or_1_out;
  wire [23:0] bit_extender_1_out;
  wire [31:0] c, c___1, c___1_t, divider_1_rem, memory_1_data_out, multiplexer_1_out, multiplexer_2_out,
       multiplexer_3_out, n, n___10, n___10___48;

  Multiplexer #(.width(32), .enable("false")) multiplexer_1 (
    .in0(num), .in1(n___10), .out(multiplexer_1_out), .sel(Lc_0));
  Divider #(.width(32)) divider_1 (.a(n), .b(32'ha), .out(n___10), .rem(divider_1_rem));  // open: upper
  Adder #(.width(32)) adder_1 (.a(divider_1_rem), .b(32'h30), .out(n___10___48));  // open: cin, cout
  or or_1 (or_1_out, demultiplexer_1_out0, \end );
  Register #(.width(32)) u_n (.D(multiplexer_1_out), .en(Ln), .Q(n), .clk(CLK), .clr(RST));
  D_Flip_Flop IDLE (.clk(CLK), .D(or_1_out), .Q(IDLE_q), .preset(RST));  // open: Qn, en, reset
  Demultiplexer #(.enable("false")) demultiplexer_1 (
    .out0(demultiplexer_1_out0), .out1(Ln_0), .in(IDLE_q), .sel(start));
  or or_2 (Write_ASCII, demultiplexer_3_out0, demultiplexer_2_out1);
  Multiplexer #(.width(32), .enable("false")) multiplexer_2 (
    .in0(c___1), .in1(c___1_t), .out(multiplexer_2_out), .sel(Write_ASCII));
  Adder #(.width(32)) adder_2 (.a(c), .b(32'h1), .out(c___1));  // open: cin, cout
  Subtractor #(.width(32)) subtractor_1 (.a(c), .b(32'h1), .out(c___1_t));  // open: bin, bout
  D_Flip_Flop IDLE_2 (.clk(CLK), .D(Ln_0), .Q(IDLE_2_q), .reset(RST));  // open: Qn, preset, en
  Register #(.width(32)) u_c (.D(multiplexer_2_out), .en(Lc), .Q(c), .clk(CLK), .clr(RST));
  or or_3 (Lc_0, IDLE_2_q, demultiplexer_3_out1);
  Multiplexer #(.width(32), .enable("false")) multiplexer_3 (
    .in0(c), .in1(c___1_t), .out(multiplexer_3_out), .sel(Write_ASCII));
  Comparator #(.width(32), .mode("unsigned")) comparator_1 (.a({32{1'b0}}), .b(n), .lt(_0_n));  // open: gt, eq
  Comparator #(.width(32), .mode("unsigned")) comparator_2 (.a({32{1'b0}}), .b(c), .lt(_0_c));  // open: gt, eq
  D_Flip_Flop IDLE_3 (.clk(CLK), .D(Write_ASCII), .Q(IDLE_3_q), .reset(RST));  // open: Qn, preset, en
  Demultiplexer #(.enable("false")) demultiplexer_2 (
    .out0(demultiplexer_2_out0), .out1(demultiplexer_2_out1), .in(IDLE_3_q), .sel(_0_c));
  Bit_Extender #(.in_width(32), .out_width(24)) bit_extender_1 (.in(multiplexer_3_out), .out(bit_extender_1_out));
  D_Flip_Flop IDLE_4 (.clk(CLK), .D(Lc_0), .Q(IDLE_4_q), .reset(RST));  // open: Qn, preset, en
  or or_4 (Lc, Lc_0, Write_ASCII);
  or or_5 (Ln, Ln_0, Lc_0);
  Demultiplexer #(.enable("false")) demultiplexer_3 (
    .out0(demultiplexer_3_out0), .out1(demultiplexer_3_out1), .in(IDLE_4_q), .sel(_0_n));
  D_Flip_Flop IDLE_5 (.clk(CLK), .D(demultiplexer_2_out0), .Q(\end ), .reset(RST));  // open: Qn, preset, en
  MEMORY memory_1 (
    .DIR(bit_extender_1_out), .DATA_IN(n___10___48), .WRITE(Lc_0), .CLK(CLK), .CLR(RST),
    .DATA_OUT(memory_1_data_out));
  Bit_Extender #(.in_width(32), .out_width(7)) bit_extender_2 (.in(memory_1_data_out), .out(ASCII));

  // Other names for the same wires on the sheet: Lc_1 = Write_ASCII; Sc = Write_ASCII; Ln_1 = Lc_0; Sn = Lc_0;
  //   Write = Lc_0
endmodule

module PRINT_DEC (
  input  [31:0] num,
  input  start,
  input  CLK,
  input  RST,
  output [6:0] ASCII,
  output Write_ASCII,
  output END
);

  wire demultiplexer_1_out0, demultiplexer_1_out1, demultiplexer_2_out0, demultiplexer_3_out0, end_t,
       IDLE_3_q, IDLE_q, or_1_out, or_2_out, or_3_out, S_ASCII, startUDEC, Write_ASCII_1;
  wire [6:0] ASCII_t;
  wire [31:0] multiplexer_1_out, negator_1_out;

  or or_1 (or_1_out, demultiplexer_1_out0, END);
  Negator #(.width(32)) negator_1 (.in(num), .out(negator_1_out));
  D_Flip_Flop IDLE (.clk(CLK), .D(or_1_out), .Q(IDLE_q), .preset(RST));  // open: Qn, en, reset
  Demultiplexer #(.enable("false")) demultiplexer_1 (
    .out0(demultiplexer_1_out0), .out1(demultiplexer_1_out1), .in(IDLE_q), .sel(start));
  Multiplexer #(.width(32), .enable("false")) multiplexer_1 (
    .in0(num), .in1(negator_1_out), .out(multiplexer_1_out), .sel(num[31]));
  Demultiplexer #(.enable("false")) demultiplexer_2 (
    .out0(demultiplexer_2_out0), .out1(S_ASCII), .in(demultiplexer_1_out1), .sel(num[31]));
  or or_2 (or_2_out, demultiplexer_2_out0, S_ASCII);
  D_Flip_Flop IDLE_2 (.clk(CLK), .D(or_2_out), .Q(startUDEC), .reset(RST));  // open: Qn, preset, en
  PRINT_UDEC print_udec_1 (
    .num(multiplexer_1_out), .start(startUDEC), .CLK(CLK), .RST(RST), .ASCII(ASCII_t),
    .Write_ASCII(Write_ASCII_1), .\end (end_t));
  D_Flip_Flop IDLE_3 (.clk(CLK), .D(or_3_out), .Q(IDLE_3_q), .reset(RST));  // open: Qn, preset, en
  or or_3 (or_3_out, startUDEC, demultiplexer_3_out0);
  Demultiplexer #(.enable("false")) demultiplexer_3 (
    .out0(demultiplexer_3_out0), .out1(END), .in(IDLE_3_q), .sel(end_t));
  Multiplexer #(.width(7), .enable("false")) multiplexer_2 (
    .in0(ASCII_t), .in1(7'b0101101), .out(ASCII), .sel(S_ASCII));
  or or_4 (Write_ASCII, S_ASCII, Write_ASCII_1);

  // Other names for the same wires on the sheet: sign = num[31]; Write_ASCII_0 = S_ASCII
endmodule

module TEST_PRINT (
  input  [31:0] in_1,
  output out_2
);

  wire button_1_out, button_2_out, CLK, CLR, d_ff_1_q, Write_ASCII;
  wire [6:0] ASCII;

  Button button_1 (.out(button_1_out));
  Clock clock_1 (.out(CLK));
  D_Flip_Flop d_ff_1 (.clk(CLK), .D(1'b1), .Q(d_ff_1_q), .reset(button_1_out));  // open: Qn, preset, en
  D_Flip_Flop d_ff_2 (.clk(CLK), .D(d_ff_1_q), .Qn(CLR), .reset(button_1_out));  // open: Q, preset, en
  Button button_2 (.out(button_2_out));
  PRINT_UDEC print_udec_1 ();  // open: num, start, CLK, RST, ASCII, Write_ASCII, end
  PRINT_DEC print_dec_1 (
    .num(in_1), .start(button_2_out), .CLK(CLK), .RST(CLR), .ASCII(ASCII), .Write_ASCII(Write_ASCII),
    .END(out_2));
  TTY #(.rows(32), .cols(60)) tty_1 (.data(ASCII), .clk(CLK), .we(Write_ASCII), .clr(CLR));
endmodule

module Data_Path (
  input  [31:0] day,
  input  [31:0] month,
  input  [31:0] year,
  input  Start,
  output final_final_true_output
);

  wire _1output, _2output, _3output, _4output, _5output, _6output, _7output, _8output, _9output, _10output,
       _11output, _12output, _22output, _28, _29, _30, _31, anno_bisiesto, comparator_9_eq, comparator_10_eq,
       demultiplexer_1_out1, demultiplexer_1_out2, demultiplexer_1_out3, demultiplexer_1_out4,
       demultiplexer_1_out5, demultiplexer_1_out6, demultiplexer_1_out7, demultiplexer_1_out8,
       demultiplexer_1_out9, demultiplexer_1_out10, demultiplexer_1_out11, demultiplexer_1_out12,
       demultiplexer_2_out0, demultiplexer_2_out1, final_output1, final_output2, not_1_out, or_1_out,
       output1, output2, output3, output4;
  wire [31:0] divider_1_rem, divider_2_rem;

  Demultiplexer #(.select(4), .enable("false")) demultiplexer_1 (
    .out1(demultiplexer_1_out1), .out2(demultiplexer_1_out2), .out3(demultiplexer_1_out3),
    .out4(demultiplexer_1_out4), .out5(demultiplexer_1_out5), .out6(demultiplexer_1_out6),
    .out7(demultiplexer_1_out7), .out8(demultiplexer_1_out8), .out9(demultiplexer_1_out9),
    .out10(demultiplexer_1_out10), .out11(demultiplexer_1_out11), .out12(demultiplexer_1_out12), .in(1'b1),
    .sel(month[3:0]));  // open: out0, out13, out14, out15
  Comparator #(.width(32), .mode("unsigned")) comparator_1 (.a(month), .b(32'h1), .lt(output1));  // open: gt, eq
  Comparator #(.width(32), .mode("unsigned")) comparator_2 (.a(month), .b(32'hc), .gt(output4));  // open: eq, lt
  Comparator #(.width(32), .mode("unsigned")) comparator_3 (.a(year), .b({32{1'b0}}), .lt(output2));  // open: gt, eq
  Comparator #(.width(32), .mode("unsigned")) comparator_4 (.a(day), .b(32'h1), .lt(output3));  // open: gt, eq
  Divider #(.width(32)) divider_1 (.a(year), .b(32'h4), .rem(divider_1_rem));  // open: out, upper
  Divider #(.width(32)) divider_2 (.a(year), .b(32'h64), .rem(divider_2_rem));  // open: out, upper
  Comparator #(.width(32), .mode("unsigned")) comparator_5 (.a(day), .b(32'h20), .lt(_31));  // open: gt, eq
  Comparator #(.width(32), .mode("unsigned")) comparator_6 (.a(day), .b(32'h1f), .lt(_30));  // open: gt, eq
  Comparator #(.width(32), .mode("unsigned")) comparator_7 (.a(day), .b(32'h1e), .lt(_29));  // open: gt, eq
  Comparator #(.width(32), .mode("unsigned")) comparator_8 (.a(day), .b(32'h1d), .lt(_28));  // open: gt, eq
  Comparator #(.width(32), .mode("unsigned")) comparator_9 (
    .a(divider_1_rem), .b({32{1'b0}}), .eq(comparator_9_eq));  // open: gt, lt
  Comparator #(.width(32), .mode("unsigned")) comparator_10 (
    .a(divider_2_rem), .b({32{1'b0}}), .eq(comparator_10_eq));  // open: gt, lt
  and and_1 (anno_bisiesto, comparator_9_eq, not_1_out);
  not not_1 (not_1_out, comparator_10_eq);
  and and_2 (_12output, demultiplexer_1_out12, _31);
  and and_3 (_10output, demultiplexer_1_out10, _31);
  and and_4 (_11output, demultiplexer_1_out11, _30);
  or or_1 (or_1_out, output2, output1, output3, output4);
  not not_2 (final_output1, or_1_out);
  and and_5 (final_final_true_output, final_output1, final_output2, Start);
  and and_6 (_8output, demultiplexer_1_out8, _31);
  and and_7 (_9output, demultiplexer_1_out9, _30);
  or or_2 (final_output2, _1output, _2output, _22output, _3output, _4output, _5output, _6output, _7output, _8output, _9output, _10output, _11output, _12output);
  and and_8 (_6output, demultiplexer_1_out6, _30);
  and and_9 (_7output, demultiplexer_1_out7, _31);
  and and_10 (_5output, demultiplexer_1_out5, _31);
  and and_11 (_4output, demultiplexer_1_out4, _30);
  and and_12 (_3output, demultiplexer_1_out3, _31);
  and and_13 (_22output, _28, demultiplexer_2_out0);
  and and_14 (_1output, demultiplexer_1_out1, _31);
  Demultiplexer #(.enable("false")) demultiplexer_2 (
    .out0(demultiplexer_2_out0), .out1(demultiplexer_2_out1), .in(demultiplexer_1_out2), .sel(anno_bisiesto));
  and and_15 (_2output, demultiplexer_2_out1, _29);
endmodule

module Control_Unit (
  input  Start,
  input  rst,
  input  clk,
  output Calculate,
  output End
);

  wire demultiplexer_1_out0, IDLE_q, or_1_out;

  D_Flip_Flop IDLE (.clk(clk), .D(demultiplexer_1_out0), .Q(IDLE_q), .preset(rst));  // open: Qn, en, reset
  Demultiplexer #(.enable("false")) demultiplexer_1 (
    .out0(demultiplexer_1_out0), .out1(Calculate), .in(IDLE_q), .sel(Start));
  or or_1 (or_1_out, End, Calculate);
  D_Flip_Flop u_END (.clk(clk), .D(or_1_out), .Q(End), .reset(rst));  // open: Qn, preset, en

  // Other names for the same wires on the sheet: reset = rst
endmodule
