// Logisim project BigASM_Tribonacci.circ as structural Verilog
module BOARD_BIG_ASM (
  output out_1
);

  wire button_1_out, CLK, CLR, d_ff_1_q, not_1_out, Write, Write_ASCII;
  wire [6:0] ASCII;
  wire [7:0] counter_1_q;
  wire [23:0] Dir_INPUT, Dir_MEMORY;
  wire [31:0] INPUT, MEMORY_IN, MEMORY_OUT;

  Button button_1 (.out(button_1_out));
  Clock clock_1 (.out(CLK));
  D_Flip_Flop d_ff_1 (.clk(CLK), .D(1'b1), .Q(d_ff_1_q), .reset(button_1_out));  // open: Qn, preset, en
  D_Flip_Flop d_ff_2 (.clk(CLK), .D(d_ff_1_q), .Qn(CLR), .reset(button_1_out));  // open: Q, preset, en
  BIG_ASM big_asm_1 (
    .DATA_INPUT(INPUT), .MEMORY_IN(MEMORY_OUT), .CLK(CLK), .CLR(CLR), .DIR_INPUT(Dir_INPUT),
    .MEMORY_OUT(MEMORY_IN), .DIR_MEMORY(Dir_MEMORY), .Write_OUTPUT(Write), .ASCII(ASCII),
    .Write_ASCII(Write_ASCII), .END(out_1));
  MEMORY memory_1 (.DIR(Dir_MEMORY), .DATA_IN(MEMORY_IN), .WRITE(Write), .CLK(CLK), .CLR(CLR), .DATA_OUT(MEMORY_OUT));
  INPUT input_1 (.DIR(Dir_INPUT), .CLK(CLK), .DATA_OUT(INPUT));
  Counter counter_1 (.load(1'b0), .count(not_1_out), .Q(counter_1_q), .clk(CLK), .clr(CLR));  // open: D, carry
  not not_1 (not_1_out, out_1);
  // Probe on counter_1_q
  TTY #(.rows(32), .cols(60)) tty_1 (.data(ASCII), .clk(CLK), .we(Write_ASCII), .clr(CLR));

  // Other names for the same wires on the sheet: END = out_1

  // Notes on the sheet:
  //   COUNTER
  //   BOARD
endmodule

module INPUT (
  input  [23:0] DIR,
  input  CLK,
  output [31:0] DATA_OUT
);

  RAM #(.addrWidth(24), .dataWidth(32)) ram_1 (.addr(DIR), .data(DATA_OUT), .clk(CLK), .ld(1'b1));  // open: sel, clr
endmodule

module MEMORY (
  input  [23:0] DIR,
  input  [31:0] DATA_IN,
  input  WRITE,
  input  CLK,
  input  CLR,
  output [31:0] DATA_OUT
);

  RAM #(.addrWidth(24), .dataWidth(32), .bus("separate")) ram_1 (
    .addr(DIR), .din(DATA_IN), .data(DATA_OUT), .str(WRITE), .clk(CLK), .clr(CLR));  // open: sel, ld
endmodule

module BIG_ASM (
  input  [31:0] DATA_INPUT,
  input  [31:0] MEMORY_IN,
  input  CLK,
  input  CLR,
  output [23:0] DIR_INPUT,
  output [31:0] MEMORY_OUT,
  output [23:0] DIR_MEMORY,
  output Write_OUTPUT,
  output [6:0] ASCII,
  output Write_ASCII,
  output END
);

  wire control_unit_1_out_6, control_unit_1_out_10, control_unit_1_out_11, control_unit_1_out_12,
       control_unit_1_out_13, n_2, n__3, PRINT;
  wire [1:0] control_unit_1_sa, control_unit_1_sb, control_unit_1_sc;
  wire [31:0] a;

  Control_Unit control_unit_1 (
    .out_6(control_unit_1_out_6), .out_10(control_unit_1_out_10), .in_5(CLK), .out_11(control_unit_1_out_11),
    .out_12(control_unit_1_out_12), .in_4(CLR), .out_13(control_unit_1_out_13), .in_1(a),
    .Sa(control_unit_1_sa), .Sb(control_unit_1_sb), .in_2(n__3), .Sc(control_unit_1_sc), .in_3(n_2),
    .out_14(PRINT));
  Data_Path data_path_1 (
    .in_1(DATA_INPUT), .in_2(control_unit_1_out_6), .in_3(control_unit_1_sa), .in_4(control_unit_1_sb),
    .in_5(control_unit_1_sc), .in_6(control_unit_1_out_10), .in_7(control_unit_1_out_11),
    .in_8(control_unit_1_out_12), .in_9(control_unit_1_out_13), .in_10(CLK), .out_11(a), .out_12(n__3),
    .out_13(n_2));
  PRINT_DEC print_dec_1 (
    .num(a), .start(PRINT), .CLK(CLK), .RST(CLR), .ASCII(ASCII), .Write_ASCII(Write_ASCII), .END(END));

  assign DIR_INPUT = {24{1'b0}};
  assign DIR_MEMORY = {24{1'b0}};
  assign MEMORY_OUT = {32{1'b0}};
  assign Write_OUTPUT = 1'b0;

  // Other names for the same wires on the sheet: N[31:0] = DATA_INPUT; Reset = CLR

  // Notes on the sheet:
  //   Conection
  //   Print
endmodule

module PRINT_UDEC (
  input  [31:0] num,
  input  start,
  input  CLK,
  input  RST,
  output [6:0] ASCII,
  output Write_ASCII,
  output \end 
);

  wire _0_c, _0_n, demultiplexer_1_out0, demultiplexer_2_out0, demultiplexer_2_out1, demultiplexer_3_out0,
       demultiplexer_3_out1, IDLE_2_q, IDLE_3_q, IDLE_4_q, IDLE_q, Lc, Lc_0, Ln, Ln_0, or_1_out;
  wire [23:0] bit_extender_1_out;
  wire [31:0] c, c___1, c___1_t, divider_1_rem, memory_1_data_out, multiplexer_1_out, multiplexer_2_out,
       multiplexer_3_out, n, n___10, n___10___48;

  Multiplexer #(.width(32), .enable("false")) multiplexer_1 (
    .in0(num), .in1(n___10), .out(multiplexer_1_out), .sel(Lc_0));
  Divider #(.width(32)) divider_1 (.a(n), .b(32'ha), .out(n___10), .rem(divider_1_rem));  // open: upper
  Adder #(.width(32)) adder_1 (.a(divider_1_rem), .b(32'h30), .out(n___10___48));  // open: cin, cout
  or or_1 (or_1_out, demultiplexer_1_out0, \end );
  Register #(.width(32)) u_n (.D(multiplexer_1_out), .en(Ln), .Q(n), .clk(CLK), .clr(RST));
  D_Flip_Flop IDLE (.clk(CLK), .D(or_1_out), .Q(IDLE_q), .preset(RST));  // open: Qn, en, reset
  Demultiplexer #(.enable("false")) demultiplexer_1 (
    .out0(demultiplexer_1_out0), .out1(Ln_0), .in(IDLE_q), .sel(start));
  or or_2 (Write_ASCII, demultiplexer_3_out0, demultiplexer_2_out1);
  Multiplexer #(.width(32), .enable("false")) multiplexer_2 (
    .in0(c___1), .in1(c___1_t), .out(multiplexer_2_out), .sel(Write_ASCII));
  Adder #(.width(32)) adder_2 (.a(c), .b(32'h1), .out(c___1));  // open: cin, cout
  Subtractor #(.width(32)) subtractor_1 (.a(c), .b(32'h1), .out(c___1_t));  // open: bin, bout
  D_Flip_Flop IDLE_2 (.clk(CLK), .D(Ln_0), .Q(IDLE_2_q), .reset(RST));  // open: Qn, preset, en
  Register #(.width(32)) u_c (.D(multiplexer_2_out), .en(Lc), .Q(c), .clk(CLK), .clr(RST));
  or or_3 (Lc_0, IDLE_2_q, demultiplexer_3_out1);
  Multiplexer #(.width(32), .enable("false")) multiplexer_3 (
    .in0(c), .in1(c___1_t), .out(multiplexer_3_out), .sel(Write_ASCII));
  Comparator #(.width(32), .mode("unsigned")) comparator_1 (.a({32{1'b0}}), .b(n), .lt(_0_n));  // open: gt, eq
  Comparator #(.width(32), .mode("unsigned")) comparator_2 (.a({32{1'b0}}), .b(c), .lt(_0_c));  // open: gt, eq
  D_Flip_Flop IDLE_3 (.clk(CLK), .D(Write_ASCII), .Q(IDLE_3_q), .reset(RST));  // open: Qn, preset, en
  Demultiplexer #(.enable("false")) demultiplexer_2 (
    .out0(demultiplexer_2_out0), .out1(demultiplexer_2_out1), .in(IDLE_3_q), .sel(_0_c));
  Bit_Extender #(.in_width(32), .out_width(24)) bit_extender_1 (.in(multiplexer_3_out), .out(bit_extender_1_out));
  D_Flip_Flop IDLE_4 (.clk(CLK), .D(Lc_0), .Q(IDLE_4_q), .reset(RST));  // open: Qn, preset, en
  or or_4 (Lc, Lc_0, Write_ASCII);
  or or_5 (Ln, Ln_0, Lc_0);
  Demultiplexer #(.enable("false")) demultiplexer_3 (
    .out0(demultiplexer_3_out0), .out1(demultiplexer_3_out1), .in(IDLE_4_q), .sel(_0_n));
  D_Flip_Flop IDLE_5 (.clk(CLK), .D(demultiplexer_2_out0), .Q(\end ), .reset(RST));  // open: Qn, preset, en
  MEMORY memory_1 (
    .DIR(bit_extender_1_out), .DATA_IN(n___10___48), .WRITE(Lc_0), .CLK(CLK), .CLR(RST),
    .DATA_OUT(memory_1_data_out));
  Bit_Extender #(.in_width(32), .out_width(7)) bit_extender_2 (.in(memory_1_data_out), .out(ASCII));

  // Other names for the same wires on the sheet: Lc_1 = Write_ASCII; Sc = Write_ASCII; Ln_1 = Lc_0; Sn = Lc_0;
  //   Write = Lc_0
endmodule

module PRINT_DEC (
  input  [31:0] num,
  input  start,
  input  CLK,
  input  RST,
  output [6:0] ASCII,
  output Write_ASCII,
  output END
);

  wire demultiplexer_1_out0, demultiplexer_1_out1, demultiplexer_2_out0, demultiplexer_3_out0, end_t,
       IDLE_3_q, IDLE_q, or_1_out, or_2_out, or_3_out, S_ASCII, startUDEC, Write_ASCII_1;
  wire [6:0] ASCII_t;
  wire [31:0] multiplexer_1_out, negator_1_out;

  or or_1 (or_1_out, demultiplexer_1_out0, END);
  Negator #(.width(32)) negator_1 (.in(num), .out(negator_1_out));
  D_Flip_Flop IDLE (.clk(CLK), .D(or_1_out), .Q(IDLE_q), .preset(RST));  // open: Qn, en, reset
  Demultiplexer #(.enable("false")) demultiplexer_1 (
    .out0(demultiplexer_1_out0), .out1(demultiplexer_1_out1), .in(IDLE_q), .sel(start));
  Multiplexer #(.width(32), .enable("false")) multiplexer_1 (
    .in0(num), .in1(negator_1_out), .out(multiplexer_1_out), .sel(num[31]));
  Demultiplexer #(.enable("false")) demultiplexer_2 (
    .out0(demultiplexer_2_out0), .out1(S_ASCII), .in(demultiplexer_1_out1), .sel(num[31]));
  or or_2 (or_2_out, demultiplexer_2_out0, S_ASCII);
  D_Flip_Flop IDLE_2 (.clk(CLK), .D(or_2_out), .Q(startUDEC), .reset(RST));  // open: Qn, preset, en
  PRINT_UDEC print_udec_1 (
    .num(multiplexer_1_out), .start(startUDEC), .CLK(CLK), .RST(RST), .ASCII(ASCII_t),
    .Write_ASCII(Write_ASCII_1), .\end (end_t));
  D_Flip_Flop IDLE_3 (.clk(CLK), .D(or_3_out), .Q(IDLE_3_q), .reset(RST));  // open: Qn, preset, en
  or or_3 (or_3_out, startUDEC, demultiplexer_3_out0);
  Demultiplexer #(.enable("false")) demultiplexer_3 (
    .out0(demultiplexer_3_out0), .out1(END), .in(IDLE_3_q), .sel(end_t));
  Multiplexer #(.width(7), .enable("false")) multiplexer_2 (
    .in0(ASCII_t), .in1(7'b0101101), .out(ASCII), .sel(S_ASCII));
  or or_4 (Write_ASCII, S_ASCII, Write_ASCII_1);

  // Other names for the same wires on the sheet: sign = num[31]; Write_ASCII_0 = S_ASCII
endmodule

module TEST_PRINT (
  input  [31:0] in_1,
  output out_2
);

  wire button_1_out, button_2_out, CLK, CLR, d_ff_1_q, Write_ASCII;
  wire [6:0] ASCII;

  Button button_1 (.out(button_1_out));
  Clock clock_1 (.out(CLK));
  D_Flip_Flop d_ff_1 (.clk(CLK), .D(1'b1), .Q(d_ff_1_q), .reset(button_1_out));  // open: Qn, preset, en
  D_Flip_Flop d_ff_2 (.clk(CLK), .D(d_ff_1_q), .Qn(CLR), .reset(button_1_out));  // open: Q, preset, en
  Button button_2 (.out(button_2_out));
  PRINT_UDEC print_udec_1 ();  // open: num, start, CLK, RST, ASCII, Write_ASCII, end
  PRINT_DEC print_dec_1 (
    .num(in_1), .start(button_2_out), .CLK(CLK), .RST(CLR), .ASCII(ASCII), .Write_ASCII(Write_ASCII),
    .END(out_2));
  TTY #(.rows(32), .cols(60)) tty_1 (.data(ASCII), .clk(CLK), .we(Write_ASCII), .clr(CLR));
endmodule

module Data_Path (
  input  [31:0] in_1,
  input  in_2,
  input  [1:0] in_3,
  input  [1:0] in_4,
  input  [1:0] in_5,
  input  in_6,
  input  in_7,
  input  in_8,
  input  in_9,
  input  in_10,
  output [31:0] out_11,
  output out_12,
  output out_13
);

  wire [31:0] a_b_c, adder_1_out, b, c, multiplexer_1_out, multiplexer_2_out, multiplexer_3_out,
       multiplexer_4_out, n, n_1;

  Multiplexer #(.select(2), .width(32), .enable("false")) multiplexer_1 (
    .in0(32'h1), .in1(b), .in2({32{1'b0}}), .out(multiplexer_1_out), .sel(in_3));  // open: in3
  Multiplexer #(.select(2), .width(32), .enable("false")) multiplexer_2 (
    .in0({32{1'b0}}), .in1(c), .in2(out_11), .out(multiplexer_2_out), .sel(in_4));  // open: in3
  Multiplexer #(.select(2), .width(32), .enable("false")) multiplexer_3 (
    .in0({32{1'b0}}), .in1(a_b_c), .in2(b), .out(multiplexer_3_out), .sel(in_5));  // open: in3
  Multiplexer #(.width(32), .enable("false")) multiplexer_4 (
    .in0(in_1), .in1(n_1), .out(multiplexer_4_out), .sel(in_2));
  Register #(.width(32)) register_1 (.D(multiplexer_1_out), .en(in_7), .Q(out_11), .clk(in_10));  // open: clr
  Register #(.width(32)) register_2 (.D(multiplexer_2_out), .en(in_8), .Q(b), .clk(in_10));  // open: clr
  Register #(.width(32)) register_3 (.D(multiplexer_3_out), .en(in_9), .Q(c), .clk(in_10));  // open: clr
  Register #(.width(32)) register_4 (.D(multiplexer_4_out), .en(in_6), .Q(n), .clk(in_10));  // open: clr
  Adder #(.width(32)) adder_1 (.a(out_11), .b(b), .out(adder_1_out));  // open: cin, cout
  Subtractor #(.width(32)) subtractor_1 (.a(n), .b(32'h1), .out(n_1));  // open: bin, bout
  Comparator #(.width(32), .mode("unsigned")) comparator_1 (.a(n), .b(32'h2), .gt(out_12));  // open: eq, lt
  Comparator #(.width(32), .mode("unsigned")) comparator_2 (.a(n), .b(32'h1), .lt(out_13));  // open: gt, eq
  Adder #(.width(32)) adder_2 (.a(adder_1_out), .b(c), .out(a_b_c));  // open: cin, cout

  // Other names for the same wires on the sheet: a[31:0] = out_11; Clk = in_10; La = in_7; Lb = in_8; Lc = in_9;
  //   Ln = in_6; n_2 = out_12; n__1 = out_13; n_input[31:0] = in_1; Sa[1:0] = in_3; Sb[1:0] = in_4; Sc[1:0] = in_5;
  //   Sn = in_2

  // Notes on the sheet:
  //   INPUT
  //   Asignations
  //   Flags
  //   Arithmetics_Operations
  //   Output
endmodule

module Control_Unit (
  input  [31:0] in_1,
  input  in_2,
  input  in_3,
  input  in_4,
  input  in_5,
  output out_6,
  output [1:0] Sa,
  output [1:0] Sb,
  output [1:0] Sc,
  output out_10,
  output out_11,
  output out_12,
  output out_13,
  output out_14
);

  wire demultiplexer_1_out0, demultiplexer_2_out0, demultiplexer_3_out0, demultiplexer_4_out0,
       demultiplexer_4_out1, IDDLE_q, La1, or_1_out, or_2_out, or_3_out, or_4_out, Start, WHILE_2_q,
       WHILE_3_q, WHILE_q;

  D_Flip_Flop IDDLE (.clk(in_5), .D(demultiplexer_1_out0), .Q(IDDLE_q), .preset(in_4));  // open: Qn, en, reset
  Demultiplexer #(.enable("false")) demultiplexer_1 (
    .out0(demultiplexer_1_out0), .out1(La1), .in(or_1_out), .sel(Start));
  or or_1 (or_1_out, demultiplexer_4_out1, IDDLE_q);
  D_Flip_Flop IDDLE_2 (.clk(in_5), .D(in_4), .Q(Start));  // open: Qn, preset, en, reset
  or or_2 (or_2_out, La1, out_6);
  D_Flip_Flop WHILE (.clk(in_5), .D(or_2_out), .Q(WHILE_q), .reset(in_4));  // open: Qn, preset, en
  Demultiplexer #(.enable("false")) demultiplexer_2 (
    .out0(demultiplexer_2_out0), .out1(Sc[0]), .in(WHILE_q), .sel(in_2));
  D_Flip_Flop WHILE_2 (.clk(in_5), .D(demultiplexer_2_out0), .Q(WHILE_2_q), .reset(in_4));  // open: Qn, preset, en
  Demultiplexer #(.enable("false")) demultiplexer_3 (
    .out0(demultiplexer_3_out0), .out1(Sa[1]), .in(WHILE_2_q), .sel(in_3));
  D_Flip_Flop STEP1 (.clk(in_5), .D(Sc[0]), .Q(Sb[0]), .reset(in_4));  // open: Qn, preset, en
  or or_3 (or_3_out, demultiplexer_3_out0, Sa[1]);
  D_Flip_Flop PRINT (.clk(in_5), .D(or_3_out), .Q(out_14), .reset(in_4));  // open: Qn, preset, en
  D_Flip_Flop STEP2 (.clk(in_5), .D(Sb[0]), .Q(out_6), .reset(in_4));  // open: Qn, preset, en
  or or_4 (or_4_out, demultiplexer_4_out0, out_14);
  D_Flip_Flop WHILE_3 (.clk(in_5), .D(or_4_out), .Q(WHILE_3_q), .reset(in_4));  // open: Qn, preset, en
  Demultiplexer #(.enable("false")) demultiplexer_4 (
    .out0(demultiplexer_4_out0), .out1(demultiplexer_4_out1), .in(WHILE_3_q), .sel(Start));
  or or_5 (out_10, La1, out_6);
  or or_6 (out_11, La1, Sa[1], out_6);
  or or_7 (out_12, La1, Sb[0], out_6);
  or or_8 (out_13, La1, Sb[0], Sc[0]);

  assign Sa[0] = out_6;
  assign Sb[1] = out_6;
  assign Sc[1] = Sb[0];

  // Other names for the same wires on the sheet: a[31:0] = in_1; Clk = in_5; Lb1 = La1; Lc1 = La1; Ln1 = La1;
  //   n_1 = in_3; n_2 = in_2; Out = out_14; Reset = in_4; a1 = Sa[1]; La = Sa[1]; a0 = out_6; b1 = out_6; La2 = out_6;
  //   Lb2 = out_6; Ln2 = out_6; Sn = out_6; c0 = Sc[0]; Lc2 = Sc[0]; b0 = Sb[0]; c1 = Sb[0]; Lb = Sb[0]; Lc = Sb[0]

  // Notes on the sheet:
  //   Input
  //   OUTPUT
endmodule
